// Logisim project project.circ as structural Verilog: 1 circuit, main circuit main
module main (
);

  wire Add_out, and_1_out, and_2_out, and_3_out, and_4_out, and_5_out, and_6_out, and_7_out, and_8_out,
       and_9_out, and_10_out, and_11_out, and_12_out, and_13_out, and_14_out, and_15_out, and_16_out,
       and_17_out, and_18_out, and_19_out, and_20_out, and_21_out, and_22_out, and_23_out, and_24_out,
       and_25_out, and_26_out, and_27_out, and_28_out, and_29_out, and_30_out, and_31_out, and_32_out,
       and_33_out, and_34_out, and_35_out, and_36_out, and_37_out, and_38_out, and_39_out, and_40_out,
       and_41_out, and_42_out, and_43_out, and_44_out, and_45_out, and_46_out, and_47_out, and_48_out,
       and_49_out, and_50_out, and_51_out, and_52_out, and_53_out, and_54_out, and_55_out, and_56_out,
       and_57_out, and_58_out, and_59_out, and_60_out, and_61_out, and_62_out, and_63_out, and_64_out,
       and_65_out, and_66_out, and_67_out, and_68_out, and_69_out, and_70_out, and_71_out, and_72_out,
       and_73_out, and_74_out, and_75_out, and_76_out, and_77_out, and_78_out, and_79_out, and_80_out,
       and_81_out, and_82_out, and_83_out, and_84_out, and_85_out, and_86_out, and_87_out, and_88_out,
       and_89_out, and_90_out, and_91_out, and_92_out, and_93_out, and_94_out, and_95_out, and_96_out,
       and_97_out, and_98_out, and_99_out, and_100_out, and_101_out, and_102_out, and_103_out, and_104_out,
       and_105_out, and_106_out, and_107_out, and_108_out, and_109_out, and_110_out, and_111_out,
       and_112_out, and_113_out, and_114_out, and_115_out, and_116_out, and_117_out, and_118_out,
       and_119_out, and_120_out, and_121_out, and_122_out, and_123_out, and_124_out, and_125_out,
       and_126_out, and_127_out, and_128_out, and_129_out, and_130_out, and_131_out, and_132_out,
       and_133_out, and_134_out, and_135_out, and_136_out, and_137_out, and_138_out, and_139_out,
       and_140_out, and_141_out, and_142_out, and_143_out, and_144_out, and_145_out, and_146_out,
       and_147_out, and_148_out, and_149_out, and_150_out, and_151_out, and_152_out, and_153_out,
       and_154_out, and_155_out, and_156_out, and_157_out, and_158_out, and_159_out, and_160_out,
       and_161_out, and_162_out, and_163_out, and_164_out, and_165_out, and_166_out, and_167_out,
       and_168_out, and_169_out, and_170_out, and_171_out, and_172_out, and_173_out, and_174_out,
       and_175_out, and_176_out, and_177_out, and_178_out, and_179_out, and_180_out, and_181_out,
       and_182_out, and_183_out, and_184_out, and_185_out, and_186_out, and_187_out, and_188_out,
       and_189_out, and_190_out, and_191_out, and_192_out, and_193_out, and_194_out, and_195_out,
       and_196_out, and_197_out, and_198_out, and_199_out, and_200_out, and_201_out, and_202_out,
       and_203_out, and_204_out, and_205_out, and_206_out, and_207_out, and_208_out, and_209_out,
       and_210_out, and_211_out, and_212_out, and_213_out, and_214_out, and_215_out, and_216_out,
       and_217_out, and_218_out, and_219_out, and_220_out, and_221_out, and_222_out, and_223_out,
       and_224_out, and_225_out, and_227_out, and_229_out, and_231_out, and_233_out, and_234_out,
       and_235_out, and_236_out, and_237_out, and_238_out, and_239_out, and_240_out, and_241_out,
       and_242_out, and_243_out, and_244_out, and_245_out, and_246_out, and_247_out, and_248_out,
       and_249_out, and_250_out, and_251_out, and_252_out, and_253_out, and_254_out, and_255_out,
       and_256_out, and_257_out, and_258_out, and_259_out, and_260_out, and_261_out, and_262_out,
       and_263_out, and_264_out, and_265_out, and_266_out, and_267_out, and_268_out, b_right_out,
       buffer_1_out, buffer_2_out, buffer_3_out, buffer_4_out, buffer_5_out, buffer_6_out, clock_3_out,
       D0_out, D1_out, D2_out, D3_out, D4_out, D5_out, D6_out, D7_out, D8_out, D9_out, D10_out, D11_out,
       D12_out, D13_out, D14_out, D15_out, d_ff_1_q, d_ff_2_q, d_ff_3_q, d_ff_4_q, d_ff_5_q, d_ff_6_q,
       d_ff_7_q, d_ff_8_q, d_ff_9_q, d_ff_10_q, d_ff_11_q, d_ff_12_q, d_ff_13_q, d_ff_14_q, d_ff_15_q,
       d_ff_16_q, d_ff_17_q, d_ff_18_q, d_ff_19_q, d_ff_20_q, d_ff_21_q, d_ff_22_q, d_ff_23_q, d_ff_24_q,
       d_ff_25_q, d_ff_26_q, d_ff_27_q, d_ff_28_q, d_ff_29_q, d_ff_30_q, d_ff_31_q, d_ff_32_q, d_ff_33_q,
       d_ff_34_q, d_ff_35_q, d_ff_36_q, d_ff_37_q, d_ff_38_q, d_ff_39_q, d_ff_40_q, d_ff_41_q, d_ff_42_q,
       d_ff_43_q, d_ff_44_q, d_ff_45_q, d_ff_46_q, d_ff_47_q, d_ff_48_q, d_ff_49_q, d_ff_50_q, d_ff_51_q,
       d_ff_52_q, d_ff_53_q, d_ff_54_q, d_ff_55_q, d_ff_56_q, d_ff_57_q, d_ff_58_q, d_ff_59_q, d_ff_60_q,
       d_ff_61_q, d_ff_62_q, d_ff_63_q, d_ff_64_q, d_ff_65_q, d_ff_66_q, d_ff_67_q, d_ff_68_q, d_ff_69_q,
       d_ff_70_q, d_ff_71_q, d_ff_72_q, d_ff_73_q, d_ff_74_q, d_ff_75_q, d_ff_76_q, d_ff_77_q, d_ff_78_q,
       d_ff_79_q, d_ff_80_q, d_ff_81_q, d_ff_82_q, d_ff_83_q, d_ff_84_q, d_ff_85_q, d_ff_86_q, d_ff_87_q,
       d_ff_88_q, d_ff_89_q, Halt_out, Load_out, negative_q, not_1_out, not_2_out, not_3_out, not_4_out,
       not_5_out, not_6_out, not_7_out, not_8_out, not_9_out, not_10_out, not_11_out, not_12_out, not_13_out,
       not_14_out, not_15_out, not_16_out, not_17_out, not_18_out, not_19_out, not_20_out, not_21_out,
       not_22_out, not_23_out, not_24_out, not_25_out, not_26_out, not_27_out, not_28_out, not_29_out,
       not_30_out, not_31_out, not_32_out, not_33_out, not_34_out, not_35_out, not_36_out, not_37_out,
       not_38_out, not_39_out, not_40_out, not_41_out, not_42_out, not_43_out, not_44_out, not_45_out,
       not_46_out, not_47_out, not_48_out, not_49_out, not_50_out, not_51_out, not_52_out, not_53_out,
       not_54_out, not_55_out, not_56_out, not_57_out, not_58_out, not_59_out, not_60_out, not_61_out,
       not_62_out, not_63_out, not_64_out, not_65_out, not_66_out, not_67_out, not_68_out, not_69_out,
       not_70_out, not_71_out, not_72_out, not_73_out, not_74_out, not_75_out, not_76_out, not_77_out,
       not_78_out, not_79_out, not_80_out, not_81_out, not_82_out, not_83_out, not_84_out, not_85_out,
       not_86_out, not_87_out, not_88_out, not_89_out, not_90_out, not_91_out, not_92_out, not_93_out,
       not_94_out, not_95_out, not_96_out, not_97_out, not_98_out, not_99_out, not_100_out, not_101_out,
       not_102_out, not_103_out, not_104_out, not_105_out, not_106_out, not_107_out, not_108_out,
       not_109_out, not_110_out, not_111_out, not_112_out, not_113_out, not_114_out, not_115_out,
       not_116_out, not_117_out, not_118_out, not_119_out, not_120_out, or_1_out, or_2_out, or_3_out,
       or_4_out, or_5_out, or_6_out, or_7_out, or_8_out, or_9_out, or_10_out, or_11_out, or_12_out,
       or_13_out, or_14_out, or_15_out, or_16_out, or_17_out, or_18_out, or_19_out, or_20_out, or_21_out,
       or_22_out, or_23_out, or_24_out, or_25_out, or_26_out, or_27_out, or_28_out, or_29_out, or_30_out,
       or_31_out, or_32_out, or_33_out, or_34_out, or_35_out, or_36_out, or_37_out, or_38_out, or_39_out,
       or_40_out, or_41_out, or_42_out, or_43_out, or_44_out, or_45_out, or_46_out, or_47_out, or_48_out,
       or_49_out, or_50_out, or_51_out, or_52_out, or_53_out, or_54_out, or_55_out, or_56_out, or_57_out,
       or_58_out, or_59_out, or_60_out, or_61_out, or_62_out, or_63_out, or_64_out, or_65_out, or_66_out,
       or_67_out, or_68_out, or_69_out, or_70_out, or_71_out, or_72_out, or_73_out, or_74_out, or_75_out,
       or_76_out, or_77_out, or_78_out, or_79_out, or_80_out, or_81_out, or_82_out, or_83_out, or_84_out,
       or_85_out, or_86_out, or_87_out, or_88_out, or_89_out, or_90_out, or_91_out, or_92_out, or_93_out,
       or_94_out, or_95_out, or_96_out, or_97_out, or_98_out, or_99_out, or_100_out, or_101_out, or_102_out,
       overflow_q, S0_out, S1_out, S2_out, S3_out, Save_out, signed_overflow_q, Sub_out, t_right_out,
       xor_1_out, xor_2_out, xor_3_out, xor_4_out, xor_5_out, xor_6_out, xor_7_out, xor_8_out, xor_9_out,
       xor_10_out, xor_11_out, xor_12_out, xor_13_out, xor_14_out, xor_15_out, xor_16_out, xor_17_out,
       xor_18_out, xor_19_out, xor_20_out, zero_q;

  D_Flip_Flop d_ff_1 (.D(or_87_out), .clk(or_86_out), .Q(d_ff_1_q));  // open: Qn, preset, reset
  and and_1 (and_1_out, and_167_out, or_90_out);
  and and_2 (and_2_out, or_90_out, d_ff_2_q);
  D_Flip_Flop #(.trigger("high")) d_ff_2 (.D(and_3_out), .clk(and_25_out), .Q(d_ff_2_q));  // open: Qn, preset, reset
  and and_3 (and_3_out, and_119_out, or_91_out);
  buf buffer_1 (buffer_1_out, buffer_2_out);
  buf buffer_2 (buffer_2_out, buffer_3_out);
  buf buffer_3 (buffer_3_out, and_1_out);
  D_Flip_Flop #(.trigger("high")) d_ff_3 (.D(and_4_out), .clk(and_25_out), .Q(d_ff_3_q));  // open: Qn, preset, reset
  and and_4 (and_4_out, and_122_out, or_91_out);
  not not_1 (not_1_out, and_23_out);
  not not_2 (not_2_out, and_5_out);
  not not_3 (not_3_out, and_5_out);
  not not_4 (not_4_out, and_23_out);
  not not_5 (not_5_out, and_2_out);
  not not_6 (not_6_out, and_2_out);
  not not_7 (not_7_out, and_23_out);
  not not_8 (not_8_out, and_2_out);
  not not_9 (not_9_out, and_5_out);
  not not_10 (not_10_out, and_2_out);
  not not_11 (not_11_out, and_5_out);
  not not_12 (not_12_out, and_23_out);
  and and_5 (and_5_out, or_90_out, d_ff_3_q);
  D_Flip_Flop #(.trigger("high")) d_ff_4 (.D(and_6_out), .clk(and_25_out), .Q(d_ff_4_q));  // open: Qn, preset, reset
  and and_6 (and_6_out, and_125_out, or_91_out);
  not not_13 (not_13_out, d_ff_24_q);
  and and_7 (and_7_out, and_2_out, and_5_out, buffer_1_out, and_23_out);
  and and_8 (and_8_out, and_7_out, and_24_out);
  and and_9 (and_9_out, and_2_out, and_5_out, buffer_1_out, not_1_out);
  and and_10 (and_10_out, and_9_out, and_24_out);
  and and_11 (and_11_out, and_2_out, not_2_out, buffer_1_out, and_23_out);
  and and_12 (and_12_out, and_11_out, and_24_out);
  and and_13 (and_13_out, and_2_out, not_3_out, buffer_1_out, not_4_out);
  and and_14 (and_14_out, and_13_out, and_24_out);
  and and_15 (and_15_out, not_5_out, and_5_out, buffer_1_out, and_23_out);
  and and_16 (and_16_out, and_15_out, and_24_out);
  and and_17 (and_17_out, not_6_out, and_5_out, buffer_1_out, not_7_out);
  and and_18 (and_18_out, and_17_out, and_24_out);
  and and_19 (and_19_out, not_8_out, not_9_out, buffer_1_out, and_23_out);
  and and_20 (and_20_out, and_19_out, and_24_out);
  and and_21 (and_21_out, not_10_out, not_11_out, buffer_1_out, not_12_out);
  and and_22 (and_22_out, and_21_out, and_24_out);
  not not_14 (not_14_out, d_ff_1_q);
  and and_23 (and_23_out, or_90_out, d_ff_4_q);
  not not_15 (not_15_out, d_ff_27_q);
  not not_16 (not_16_out, d_ff_29_q);
  not not_17 (not_17_out, d_ff_40_q);
  not not_18 (not_18_out, d_ff_24_q);
  not not_19 (not_19_out, d_ff_27_q);
  and D0 (D0_out, not_13_out, not_15_out, not_16_out, not_17_out);
  and D1 (D1_out, not_18_out, not_19_out, not_20_out, d_ff_40_q);
  or or_1 (or_1_out, D10_out, D0_out);
  and and_24 (and_24_out, not_14_out, or_90_out);
  and and_25 (and_25_out, or_91_out, and_167_out);
  not not_20 (not_20_out, d_ff_29_q);
  not not_21 (not_21_out, d_ff_24_q);
  not not_22 (not_22_out, d_ff_27_q);
  not not_23 (not_23_out, d_ff_40_q);
  and D2 (D2_out, not_21_out, not_22_out, d_ff_29_q, not_23_out);
  and and_26 (and_26_out, or_89_out, and_167_out);
  and and_27 (and_27_out, and_7_out, and_24_out, and_46_out);
  D_Flip_Flop #(.trigger("high")) d_ff_5 (.D(and_27_out), .clk(and_8_out), .Q(d_ff_5_q));  // open: Qn, preset, reset
  and and_28 (and_28_out, and_9_out, and_24_out, and_46_out);
  D_Flip_Flop #(.trigger("high")) d_ff_6 (.D(and_28_out), .clk(and_10_out), .Q(d_ff_6_q));  // open: Qn, preset, reset
  and and_29 (and_29_out, and_11_out, and_24_out, and_46_out);
  D_Flip_Flop #(.trigger("high")) d_ff_7 (.D(and_29_out), .clk(and_12_out), .Q(d_ff_7_q));  // open: Qn, preset, reset
  and and_30 (and_30_out, and_13_out, and_24_out, and_46_out);
  D_Flip_Flop #(.trigger("high")) d_ff_8 (.D(and_30_out), .clk(and_14_out), .Q(d_ff_8_q));  // open: Qn, preset, reset
  and and_31 (and_31_out, and_15_out, and_24_out, and_46_out);
  D_Flip_Flop #(.trigger("high")) d_ff_9 (.D(and_31_out), .clk(and_16_out), .Q(d_ff_9_q));  // open: Qn, preset, reset
  and and_32 (and_32_out, and_17_out, and_24_out, and_46_out);
  D_Flip_Flop #(.trigger("high")) d_ff_10 (.D(and_32_out), .clk(and_18_out), .Q(d_ff_10_q));  // open: Qn, preset, reset
  and and_33 (and_33_out, and_19_out, and_24_out, and_46_out);
  D_Flip_Flop #(.trigger("high")) d_ff_11 (.D(and_33_out), .clk(and_20_out), .Q(d_ff_11_q));  // open: Qn, preset, reset
  and and_34 (and_34_out, and_21_out, and_24_out, and_46_out);
  D_Flip_Flop #(.trigger("high")) d_ff_12 (.D(and_34_out), .clk(and_22_out), .Q(d_ff_12_q));  // open: Qn, preset, reset
  not not_24 (not_24_out, not_14_out);
  and and_35 (and_35_out, and_167_out, or_62_out);
  and and_36 (and_36_out, and_131_out, or_62_out);
  not not_25 (not_25_out, d_ff_24_q);
  not not_26 (not_26_out, d_ff_27_q);
  not not_27 (not_27_out, d_ff_24_q);
  and D3 (D3_out, not_25_out, not_26_out, d_ff_29_q, d_ff_40_q);
  or or_2 (or_2_out, D9_out, D8_out, D7_out, D6_out, D5_out, D4_out, D3_out, D2_out, D1_out, D0_out);
  or or_3 (or_3_out, and_37_out, and_38_out, and_39_out, and_40_out, and_41_out, and_42_out, and_43_out, and_44_out);
  and and_37 (and_37_out, d_ff_5_q, and_7_out, not_24_out);
  and and_38 (and_38_out, d_ff_6_q, and_9_out, not_24_out);
  and and_39 (and_39_out, d_ff_7_q, and_11_out, not_24_out);
  and and_40 (and_40_out, d_ff_8_q, and_13_out, not_24_out);
  and and_41 (and_41_out, d_ff_9_q, and_15_out, not_24_out);
  and and_42 (and_42_out, d_ff_10_q, and_17_out, not_24_out);
  and and_43 (and_43_out, d_ff_11_q, and_19_out, not_24_out);
  and and_44 (and_44_out, d_ff_12_q, and_21_out, not_24_out);
  D_Flip_Flop #(.trigger("high")) d_ff_13 (.D(and_36_out), .clk(and_35_out), .Q(d_ff_13_q));  // open: Qn, preset, reset
  and and_45 (and_45_out, and_167_out, or_98_out);
  not not_28 (not_28_out, d_ff_29_q);
  not not_29 (not_29_out, d_ff_40_q);
  not not_30 (not_30_out, d_ff_24_q);
  and D4 (D4_out, not_27_out, d_ff_27_q, not_28_out, not_29_out);
  and D5 (D5_out, not_30_out, d_ff_27_q, not_32_out, d_ff_40_q);
  not not_31 (not_31_out, or_2_out);
  and and_46 (and_46_out, d_ff_13_q, buffer_4_out);
  and and_47 (and_47_out, d_ff_14_q, buffer_4_out);
  and and_48 (and_48_out, d_ff_23_q, buffer_4_out);
  D_Flip_Flop #(.trigger("high")) d_ff_14 (.D(and_49_out), .clk(and_35_out), .Q(d_ff_14_q));  // open: Qn, preset, reset
  and and_49 (and_49_out, and_136_out, or_62_out);
  not not_32 (not_32_out, d_ff_29_q);
  not not_33 (not_33_out, d_ff_24_q);
  not not_34 (not_34_out, d_ff_40_q);
  and D6 (D6_out, not_33_out, d_ff_27_q, d_ff_29_q, not_34_out);
  and and_50 (and_50_out, and_7_out, and_24_out, and_47_out);
  D_Flip_Flop #(.trigger("high")) d_ff_15 (.D(and_50_out), .clk(and_8_out), .Q(d_ff_15_q));  // open: Qn, preset, reset
  and and_51 (and_51_out, and_9_out, and_24_out, and_47_out);
  D_Flip_Flop #(.trigger("high")) d_ff_16 (.D(and_51_out), .clk(and_10_out), .Q(d_ff_16_q));  // open: Qn, preset, reset
  and and_52 (and_52_out, and_11_out, and_24_out, and_47_out);
  D_Flip_Flop #(.trigger("high")) d_ff_17 (.D(and_52_out), .clk(and_12_out), .Q(d_ff_17_q));  // open: Qn, preset, reset
  and and_53 (and_53_out, and_13_out, and_24_out, and_47_out);
  D_Flip_Flop #(.trigger("high")) d_ff_18 (.D(and_53_out), .clk(and_14_out), .Q(d_ff_18_q));  // open: Qn, preset, reset
  and and_54 (and_54_out, and_15_out, and_24_out, and_47_out);
  D_Flip_Flop #(.trigger("high")) d_ff_19 (.D(and_54_out), .clk(and_16_out), .Q(d_ff_19_q));  // open: Qn, preset, reset
  and and_55 (and_55_out, and_17_out, and_24_out, and_47_out);
  D_Flip_Flop #(.trigger("high")) d_ff_20 (.D(and_55_out), .clk(and_18_out), .Q(d_ff_20_q));  // open: Qn, preset, reset
  and and_56 (and_56_out, and_19_out, and_24_out, and_47_out);
  D_Flip_Flop #(.trigger("high")) d_ff_21 (.D(and_56_out), .clk(and_20_out), .Q(d_ff_21_q));  // open: Qn, preset, reset
  and and_57 (and_57_out, and_21_out, and_24_out, and_47_out);
  D_Flip_Flop #(.trigger("high")) d_ff_22 (.D(and_57_out), .clk(and_22_out), .Q(d_ff_22_q));  // open: Qn, preset, reset
  and and_58 (and_58_out, d_ff_26_q, buffer_4_out);
  D_Flip_Flop #(.trigger("high")) d_ff_23 (.D(and_59_out), .clk(and_35_out), .Q(d_ff_23_q));  // open: Qn, preset, reset
  and and_59 (and_59_out, and_140_out, or_62_out);
  and and_60 (and_60_out, or_98_out, or_52_out);
  D_Flip_Flop d_ff_24 (.D(and_60_out), .clk(and_45_out), .Q(d_ff_24_q));  // open: Qn, preset, reset
  not not_35 (not_35_out, d_ff_24_q);
  and D7 (D7_out, not_35_out, d_ff_27_q, d_ff_29_q, d_ff_40_q);
  or or_4 (or_4_out, D5_out, D15_out);
  or or_5 (or_5_out, D4_out, D14_out);
  _7_Segment_Display u_7_segment_display_1 (
    .f(or_2_out), .a(or_2_out), .b(t_right_out), .e(or_2_out), .d(or_2_out), .c(b_right_out));  // open: g, dp
  or b_right (b_right_out, or_2_out, not_31_out);
  D_Flip_Flop #(.trigger("high")) d_ff_25 (.D(or_3_out), .clk(and_26_out), .Q(d_ff_25_q));  // open: Qn, preset, reset
  or or_6 (or_6_out, and_61_out, and_62_out, and_63_out, and_64_out, and_65_out, and_66_out, and_67_out, and_68_out);
  and and_61 (and_61_out, d_ff_15_q, and_7_out, not_24_out);
  and and_62 (and_62_out, d_ff_16_q, and_9_out, not_24_out);
  and and_63 (and_63_out, d_ff_17_q, and_11_out, not_24_out);
  and and_64 (and_64_out, d_ff_18_q, and_13_out, not_24_out);
  and and_65 (and_65_out, d_ff_19_q, and_15_out, not_24_out);
  and and_66 (and_66_out, d_ff_20_q, and_17_out, not_24_out);
  and and_67 (and_67_out, d_ff_21_q, and_19_out, not_24_out);
  and and_68 (and_68_out, d_ff_22_q, and_21_out, not_24_out);
  D_Flip_Flop #(.trigger("high")) d_ff_26 (.D(and_69_out), .clk(and_35_out), .Q(d_ff_26_q));  // open: Qn, preset, reset
  and and_69 (and_69_out, and_143_out, or_62_out);
  and and_70 (and_70_out, or_98_out, or_53_out);
  D_Flip_Flop d_ff_27 (.D(and_70_out), .clk(and_45_out), .Q(d_ff_27_q));  // open: Qn, preset, reset
  not not_36 (not_36_out, d_ff_27_q);
  not not_37 (not_37_out, d_ff_29_q);
  not not_38 (not_38_out, d_ff_40_q);
  not not_39 (not_39_out, d_ff_27_q);
  and D8 (D8_out, d_ff_24_q, not_36_out, not_37_out, not_38_out);
  and D9 (D9_out, d_ff_24_q, not_39_out, not_42_out, d_ff_40_q);
  or or_7 (or_7_out, D3_out, D13_out);
  or t_right (t_right_out, or_2_out, not_31_out);
  D_Flip_Flop #(.trigger("high")) d_ff_28 (.D(or_6_out), .clk(and_26_out), .Q(d_ff_28_q));  // open: Qn, preset, reset
  buf buffer_4 (buffer_4_out, buffer_5_out);
  buf buffer_5 (buffer_5_out, buffer_6_out);
  buf buffer_6 (buffer_6_out, or_63_out);
  and and_71 (and_71_out, or_98_out, or_54_out);
  D_Flip_Flop d_ff_29 (.D(and_71_out), .clk(and_45_out), .Q(d_ff_29_q));  // open: Qn, preset, reset
  not not_40 (not_40_out, d_ff_27_q);
  not not_41 (not_41_out, d_ff_40_q);
  not not_42 (not_42_out, d_ff_29_q);
  and D10 (D10_out, d_ff_24_q, not_40_out, d_ff_29_q, not_41_out);
  or or_8 (or_8_out, D2_out, D12_out);
  or or_9 (or_9_out, D1_out, D11_out);
  or or_10 (or_10_out, or_4_out, D9_out, or_7_out, D6_out, or_5_out, or_8_out, D8_out);
  D_Flip_Flop #(.trigger("high")) d_ff_30 (.D(or_14_out), .clk(and_26_out), .Q(d_ff_30_q));  // open: Qn, preset, reset
  and and_72 (and_72_out, or_98_out, or_55_out);
  not not_43 (not_43_out, d_ff_27_q);
  and D11 (D11_out, d_ff_24_q, not_43_out, d_ff_29_q, d_ff_40_q);
  or or_11 (or_11_out, D9_out, or_1_out, or_4_out, D6_out, or_5_out, D8_out);
  _7_Segment_Display u_7_segment_display_2 (
    .g(or_10_out), .f(or_11_out), .a(or_15_out), .b(or_16_out), .e(or_12_out), .d(or_13_out), .c(or_17_out));  // open: dp
  or or_12 (or_12_out, or_1_out, D8_out, D6_out, or_8_out);
  D_Flip_Flop #(.trigger("high")) d_ff_31 (.D(or_18_out), .clk(and_26_out), .Q(d_ff_31_q));  // open: Qn, preset, reset
  and and_73 (and_73_out, and_7_out, and_24_out, and_48_out);
  D_Flip_Flop #(.trigger("high")) d_ff_32 (.D(and_73_out), .clk(and_8_out), .Q(d_ff_32_q));  // open: Qn, preset, reset
  and and_74 (and_74_out, and_9_out, and_24_out, and_48_out);
  D_Flip_Flop #(.trigger("high")) d_ff_33 (.D(and_74_out), .clk(and_10_out), .Q(d_ff_33_q));  // open: Qn, preset, reset
  and and_75 (and_75_out, and_11_out, and_24_out, and_48_out);
  D_Flip_Flop #(.trigger("high")) d_ff_34 (.D(and_75_out), .clk(and_12_out), .Q(d_ff_34_q));  // open: Qn, preset, reset
  and and_76 (and_76_out, and_13_out, and_24_out, and_48_out);
  D_Flip_Flop #(.trigger("high")) d_ff_35 (.D(and_76_out), .clk(and_14_out), .Q(d_ff_35_q));  // open: Qn, preset, reset
  and and_77 (and_77_out, and_15_out, and_24_out, and_48_out);
  D_Flip_Flop #(.trigger("high")) d_ff_36 (.D(and_77_out), .clk(and_16_out), .Q(d_ff_36_q));  // open: Qn, preset, reset
  and and_78 (and_78_out, and_17_out, and_24_out, and_48_out);
  D_Flip_Flop #(.trigger("high")) d_ff_37 (.D(and_78_out), .clk(and_18_out), .Q(d_ff_37_q));  // open: Qn, preset, reset
  and and_79 (and_79_out, and_19_out, and_24_out, and_48_out);
  D_Flip_Flop #(.trigger("high")) d_ff_38 (.D(and_79_out), .clk(and_20_out), .Q(d_ff_38_q));  // open: Qn, preset, reset
  and and_80 (and_80_out, and_21_out, and_24_out, and_48_out);
  D_Flip_Flop #(.trigger("high")) d_ff_39 (.D(and_80_out), .clk(and_22_out), .Q(d_ff_39_q));  // open: Qn, preset, reset
  D_Flip_Flop d_ff_40 (.D(and_72_out), .clk(and_45_out), .Q(d_ff_40_q));  // open: Qn, preset, reset
  not not_44 (not_44_out, d_ff_29_q);
  not not_45 (not_45_out, d_ff_40_q);
  and D12 (D12_out, d_ff_24_q, d_ff_27_q, not_44_out, not_45_out);
  and D13 (D13_out, d_ff_24_q, d_ff_27_q, not_46_out, d_ff_40_q);
  or or_13 (or_13_out, D6_out, or_1_out, or_7_out, D9_out, or_4_out, or_8_out, D8_out);
  or or_14 (or_14_out, and_81_out, and_82_out, and_83_out, and_84_out, and_85_out, and_86_out, and_87_out, and_88_out);
  and and_81 (and_81_out, d_ff_32_q, and_7_out, not_24_out);
  and and_82 (and_82_out, d_ff_33_q, and_9_out, not_24_out);
  and and_83 (and_83_out, d_ff_34_q, and_11_out, not_24_out);
  and and_84 (and_84_out, d_ff_35_q, and_13_out, not_24_out);
  and and_85 (and_85_out, d_ff_36_q, and_15_out, not_24_out);
  and and_86 (and_86_out, d_ff_37_q, and_17_out, not_24_out);
  and and_87 (and_87_out, d_ff_38_q, and_19_out, not_24_out);
  and and_88 (and_88_out, d_ff_39_q, and_21_out, not_24_out);
  not not_46 (not_46_out, d_ff_29_q);
  not not_47 (not_47_out, d_ff_40_q);
  and D14 (D14_out, d_ff_24_q, d_ff_27_q, d_ff_29_q, not_47_out);
  or or_15 (or_15_out, D9_out, D6_out, or_1_out, or_7_out, or_4_out, or_8_out, D7_out, D8_out);
  and D15 (D15_out, d_ff_24_q, d_ff_27_q, d_ff_29_q, d_ff_40_q);
  or or_16 (or_16_out, D8_out, or_5_out, or_1_out, or_8_out, or_7_out, or_9_out, D7_out, D9_out);
  or or_17 (or_17_out, D7_out, or_4_out, or_1_out, or_7_out, D9_out, or_5_out, or_9_out, D6_out, D8_out);
  and and_89 (and_89_out, d_ff_25_q, or_93_out);
  and and_90 (and_90_out, d_ff_28_q, or_93_out);
  and and_91 (and_91_out, d_ff_30_q, or_93_out);
  and and_92 (and_92_out, d_ff_31_q, or_93_out);
  and and_93 (and_93_out, and_7_out, and_24_out, and_58_out);
  D_Flip_Flop #(.trigger("high")) d_ff_41 (.D(and_93_out), .clk(and_8_out), .Q(d_ff_41_q));  // open: Qn, preset, reset
  and and_94 (and_94_out, and_9_out, and_24_out, and_58_out);
  D_Flip_Flop #(.trigger("high")) d_ff_42 (.D(and_94_out), .clk(and_10_out), .Q(d_ff_42_q));  // open: Qn, preset, reset
  and and_95 (and_95_out, and_11_out, and_24_out, and_58_out);
  D_Flip_Flop #(.trigger("high")) d_ff_43 (.D(and_95_out), .clk(and_12_out), .Q(d_ff_43_q));  // open: Qn, preset, reset
  and and_96 (and_96_out, and_13_out, and_24_out, and_58_out);
  D_Flip_Flop #(.trigger("high")) d_ff_44 (.D(and_96_out), .clk(and_14_out), .Q(d_ff_44_q));  // open: Qn, preset, reset
  and and_97 (and_97_out, and_15_out, and_24_out, and_58_out);
  D_Flip_Flop #(.trigger("high")) d_ff_45 (.D(and_97_out), .clk(and_16_out), .Q(d_ff_45_q));  // open: Qn, preset, reset
  and and_98 (and_98_out, and_17_out, and_24_out, and_58_out);
  D_Flip_Flop #(.trigger("high")) d_ff_46 (.D(and_98_out), .clk(and_18_out), .Q(d_ff_46_q));  // open: Qn, preset, reset
  and and_99 (and_99_out, and_19_out, and_24_out, and_58_out);
  D_Flip_Flop #(.trigger("high")) d_ff_47 (.D(and_99_out), .clk(and_20_out), .Q(d_ff_47_q));  // open: Qn, preset, reset
  and and_100 (and_100_out, and_21_out, and_24_out, and_58_out);
  D_Flip_Flop #(.trigger("high")) d_ff_48 (
    .D(and_100_out), .clk(and_22_out), .Q(d_ff_48_q));  // open: Qn, preset, reset
  Clock clock_1 ();  // open: out
  or or_18 (or_18_out, and_101_out, and_102_out, and_103_out, and_104_out, and_105_out, and_106_out, and_107_out, and_108_out);
  and and_101 (and_101_out, d_ff_41_q, and_7_out, not_24_out);
  and and_102 (and_102_out, d_ff_42_q, and_9_out, not_24_out);
  and and_103 (and_103_out, d_ff_43_q, and_11_out, not_24_out);
  and and_104 (and_104_out, d_ff_44_q, and_13_out, not_24_out);
  and and_105 (and_105_out, d_ff_45_q, and_15_out, not_24_out);
  and and_106 (and_106_out, d_ff_46_q, and_17_out, not_24_out);
  and and_107 (and_107_out, d_ff_47_q, and_19_out, not_24_out);
  and and_108 (and_108_out, d_ff_48_q, and_21_out, not_24_out);
  and and_109 (and_109_out, d_ff_12_q, or_99_out);
  and and_110 (and_110_out, d_ff_22_q, or_99_out);
  and and_111 (and_111_out, d_ff_39_q, or_99_out);
  and and_112 (and_112_out, d_ff_48_q, or_99_out);
  Clock clock_2 ();  // open: out
  or or_19 (or_19_out, 1'b0, and_109_out);
  or or_20 (or_20_out, 1'b0, and_110_out);
  or or_21 (or_21_out, 1'b0, and_111_out);
  or or_22 (or_22_out, 1'b0, and_112_out);
  or or_23 (or_23_out, and_89_out, or_19_out);
  or or_24 (or_24_out, and_90_out, or_20_out);
  or or_25 (or_25_out, or_21_out, and_91_out);
  and and_113 (and_113_out, and_167_out, or_88_out);
  and and_114 (and_114_out, or_97_out, or_52_out);
  D_Flip_Flop #(.trigger("high")) d_ff_49 (
    .D(and_114_out), .clk(and_127_out), .Q(d_ff_49_q));  // open: Qn, preset, reset
  and and_115 (and_115_out, or_65_out, d_ff_49_q);
  or or_26 (or_26_out, or_22_out, and_92_out);
  and and_116 (and_116_out, or_88_out, and_188_out);
  D_Flip_Flop #(.trigger("high")) d_ff_50 (
    .D(and_116_out), .clk(and_113_out), .Q(d_ff_50_q));  // open: Qn, preset, reset
  and and_117 (and_117_out, or_97_out, or_53_out);
  D_Flip_Flop #(.trigger("high")) d_ff_51 (
    .D(and_117_out), .clk(and_127_out), .Q(d_ff_51_q));  // open: Qn, preset, reset
  or or_27 (or_27_out, and_115_out, or_23_out);
  and and_118 (and_118_out, or_88_out, and_193_out);
  D_Flip_Flop #(.trigger("high")) d_ff_52 (
    .D(and_118_out), .clk(and_113_out), .Q(d_ff_52_q));  // open: Qn, preset, reset
  and and_119 (and_119_out, or_92_out, d_ff_50_q);
  and and_120 (and_120_out, or_97_out, or_54_out);
  D_Flip_Flop #(.trigger("high")) d_ff_53 (
    .D(and_120_out), .clk(and_127_out), .Q(d_ff_53_q));  // open: Qn, preset, reset
  and and_121 (and_121_out, or_65_out, d_ff_51_q);
  or or_28 (or_28_out, and_121_out, or_24_out);
  and and_122 (and_122_out, or_92_out, d_ff_52_q);
  and and_123 (and_123_out, or_65_out, d_ff_53_q);
  or or_29 (or_29_out, and_123_out, or_25_out);
  and and_124 (and_124_out, or_88_out, and_198_out);
  or or_30 (or_30_out, and_124_out, and_234_out);
  D_Flip_Flop #(.trigger("high")) d_ff_54 (.D(or_30_out), .clk(and_113_out), .Q(d_ff_54_q));  // open: Qn, preset, reset
  and and_125 (and_125_out, or_92_out, d_ff_54_q);
  and and_126 (and_126_out, or_97_out, or_55_out);
  and and_127 (and_127_out, and_167_out, or_97_out);
  D_Flip_Flop #(.trigger("high")) d_ff_55 (
    .D(and_126_out), .clk(and_127_out), .Q(d_ff_55_q));  // open: Qn, preset, reset
  and and_128 (and_128_out, or_65_out, d_ff_55_q);
  and and_129 (and_129_out, and_167_out, or_94_out);
  or or_31 (or_31_out, and_128_out, or_26_out);
  and and_130 (and_130_out, or_94_out, or_52_out);
  D_Flip_Flop #(.trigger("high")) d_ff_56 (
    .D(and_130_out), .clk(and_129_out), .Q(d_ff_56_q));  // open: Qn, preset, reset
  and and_131 (and_131_out, or_96_out, d_ff_56_q);
  and and_132 (and_132_out, or_95_out, or_52_out);
  D_Flip_Flop #(.trigger("high")) d_ff_57 (
    .D(and_132_out), .clk(and_146_out), .Q(d_ff_57_q));  // open: Qn, preset, reset
  and and_133 (and_133_out, or_72_out, d_ff_57_q);
  and and_134 (and_134_out, or_94_out, or_53_out);
  D_Flip_Flop #(.trigger("high")) d_ff_58 (
    .D(and_134_out), .clk(and_129_out), .Q(d_ff_58_q));  // open: Qn, preset, reset
  and and_135 (and_135_out, or_95_out, or_53_out);
  D_Flip_Flop #(.trigger("high")) d_ff_59 (
    .D(and_135_out), .clk(and_146_out), .Q(d_ff_59_q));  // open: Qn, preset, reset
  or or_32 (or_32_out, and_133_out, or_27_out);
  and and_136 (and_136_out, or_96_out, d_ff_58_q);
  and and_137 (and_137_out, or_95_out, or_54_out);
  D_Flip_Flop #(.trigger("high")) d_ff_60 (
    .D(and_137_out), .clk(and_146_out), .Q(d_ff_60_q));  // open: Qn, preset, reset
  and and_138 (and_138_out, or_72_out, d_ff_59_q);
  or or_33 (or_33_out, and_138_out, or_28_out);
  and and_139 (and_139_out, or_94_out, or_54_out);
  D_Flip_Flop #(.trigger("high")) d_ff_61 (
    .D(and_139_out), .clk(and_129_out), .Q(d_ff_61_q));  // open: Qn, preset, reset
  and and_140 (and_140_out, or_96_out, d_ff_61_q);
  and and_141 (and_141_out, or_72_out, d_ff_60_q);
  or or_34 (or_34_out, and_141_out, or_29_out);
  and and_142 (and_142_out, or_94_out, or_55_out);
  D_Flip_Flop #(.trigger("high")) d_ff_62 (
    .D(and_142_out), .clk(and_129_out), .Q(d_ff_62_q));  // open: Qn, preset, reset
  and and_143 (and_143_out, or_96_out, d_ff_62_q);
  and and_144 (and_144_out, or_95_out, or_55_out);
  D_Flip_Flop #(.trigger("high")) d_ff_63 (
    .D(and_144_out), .clk(and_146_out), .Q(d_ff_63_q));  // open: Qn, preset, reset
  and and_145 (and_145_out, or_72_out, d_ff_63_q);
  and and_146 (and_146_out, or_95_out, and_167_out);
  or or_35 (or_35_out, and_145_out, or_31_out);
  or or_36 (or_36_out, and_166_out, or_32_out);
  or or_37 (or_37_out, and_171_out, or_33_out);
  or or_38 (or_38_out, and_181_out, or_34_out);
  or or_39 (or_39_out, and_186_out, or_35_out);
  or or_40 (or_40_out, and_149_out, and_150_out);
  and and_147 (and_147_out, or_74_out, or_52_out);
  and and_148 (and_148_out, and_167_out, or_74_out);
  and and_149 (and_149_out, and_152_out, or_42_out);
  and and_150 (and_150_out, xor_1_out, or_41_out);
  D_Flip_Flop d_ff_64 (.D(and_147_out), .clk(and_148_out), .Q(d_ff_64_q));  // open: Qn, preset, reset
  and and_151 (and_151_out, or_76_out, d_ff_64_q);
  and and_152 (and_152_out, 1'b1, and_151_out);
  xor xor_1 (xor_1_out, and_152_out, or_42_out);
  xor xor_2 (xor_2_out, xor_1_out, or_41_out);
  and and_153 (and_153_out, or_74_out, or_53_out);
  D_Flip_Flop d_ff_65 (.D(and_153_out), .clk(and_148_out), .Q(d_ff_65_q));  // open: Qn, preset, reset
  and and_154 (and_154_out, or_76_out, d_ff_65_q);
  and and_155 (and_155_out, 1'b1, and_154_out);
  or or_41 (or_41_out, and_160_out, and_161_out);
  and and_156 (and_156_out, and_167_out, or_67_out);
  Clock clock_3 (.out(clock_3_out));
  and and_157 (and_157_out, or_74_out, or_54_out);
  D_Flip_Flop d_ff_66 (.D(and_157_out), .clk(and_148_out), .Q(d_ff_66_q));  // open: Qn, preset, reset
  and and_158 (and_158_out, 1'b1, and_164_out);
  and and_159 (and_159_out, 1'b1, and_168_out);
  and and_160 (and_160_out, and_155_out, or_43_out);
  and and_161 (and_161_out, xor_3_out, or_44_out);
  and and_162 (and_162_out, or_67_out, xor_2_out);
  D_Flip_Flop d_ff_67 (.D(and_162_out), .clk(and_156_out), .Q(d_ff_67_q));  // open: Qn, preset, reset
  not not_48 (not_48_out, Halt_out);
  and and_163 (and_163_out, or_74_out, or_55_out);
  and and_164 (and_164_out, or_76_out, d_ff_66_q);
  and and_165 (and_165_out, and_178_out, 1'b1, not_49_out);
  xor xor_3 (xor_3_out, and_155_out, or_43_out);
  xor xor_4 (xor_4_out, xor_3_out, or_44_out);
  and and_166 (and_166_out, or_70_out, d_ff_67_q);
  and and_167 (and_167_out, clock_3_out, not_48_out);
  D_Flip_Flop d_ff_68 (.D(and_163_out), .clk(and_148_out), .Q(d_ff_68_q));  // open: Qn, preset, reset
  and and_168 (and_168_out, or_76_out, d_ff_68_q);
  not not_49 (not_49_out, and_242_out);
  not not_50 (not_50_out, and_242_out);
  and and_169 (and_169_out, and_184_out, 1'b1, not_50_out);
  or or_42 (or_42_out, and_165_out, xor_7_out);
  or or_43 (or_43_out, and_169_out, xor_9_out);
  or or_44 (or_44_out, and_174_out, and_175_out);
  and and_170 (and_170_out, or_67_out, xor_4_out);
  D_Flip_Flop d_ff_69 (.D(and_170_out), .clk(and_156_out), .Q(d_ff_69_q));  // open: Qn, preset, reset
  and and_171 (and_171_out, or_70_out, d_ff_69_q);
  and and_172 (and_172_out, or_78_out, or_52_out);
  not not_51 (not_51_out, and_242_out);
  and and_173 (and_173_out, and_195_out, 1'b1, not_51_out);
  or or_45 (or_45_out, and_173_out, xor_11_out);
  and and_174 (and_174_out, and_158_out, or_45_out);
  and and_175 (and_175_out, xor_5_out, and_185_out);
  and and_176 (and_176_out, or_67_out, xor_6_out);
  D_Flip_Flop d_ff_70 (.D(and_176_out), .clk(and_156_out), .Q(d_ff_70_q));  // open: Qn, preset, reset
  and and_177 (and_177_out, and_167_out, or_101_out);
  D_Flip_Flop d_ff_71 (.D(and_172_out), .clk(and_203_out), .Q(d_ff_71_q));  // open: Qn, preset, reset
  and and_178 (and_178_out, or_58_out, d_ff_71_q);
  not not_52 (not_52_out, and_242_out);
  and and_179 (and_179_out, and_199_out, 1'b1, not_52_out);
  or or_46 (or_46_out, and_179_out, xor_13_out);
  xor xor_5 (xor_5_out, and_158_out, or_45_out);
  xor xor_6 (xor_6_out, xor_5_out, and_185_out);
  and and_180 (and_180_out, or_67_out, xor_8_out);
  D_Flip_Flop d_ff_72 (.D(and_180_out), .clk(and_156_out), .Q(d_ff_72_q));  // open: Qn, preset, reset
  and and_181 (and_181_out, or_70_out, d_ff_70_q);
  and and_182 (and_182_out, or_101_out, and_207_out);
  D_Flip_Flop d_ff_73 (.D(and_182_out), .clk(and_177_out), .Q(d_ff_73_q));  // open: Qn, preset, reset
  and and_183 (and_183_out, or_78_out, or_53_out);
  D_Flip_Flop d_ff_74 (.D(and_183_out), .clk(and_203_out), .Q(d_ff_74_q));  // open: Qn, preset, reset
  and and_184 (and_184_out, or_58_out, d_ff_74_q);
  not not_53 (not_53_out, and_178_out);
  xor xor_7 (xor_7_out, and_190_out, and_192_out);
  and and_185 (and_185_out, and_159_out, or_46_out);
  and and_186 (and_186_out, or_70_out, d_ff_72_q);
  and and_187 (and_187_out, or_101_out, and_212_out);
  D_Flip_Flop d_ff_75 (.D(and_187_out), .clk(and_177_out), .Q(d_ff_75_q));  // open: Qn, preset, reset
  and and_188 (and_188_out, or_102_out, d_ff_73_q);
  and and_189 (and_189_out, or_78_out, or_54_out);
  D_Flip_Flop d_ff_76 (.D(and_189_out), .clk(and_203_out), .Q(d_ff_76_q));  // open: Qn, preset, reset
  not not_54 (not_54_out, and_184_out);
  and and_190 (and_190_out, not_53_out, 1'b1, and_242_out);
  and and_191 (and_191_out, not_54_out, 1'b1, and_242_out);
  and and_192 (and_192_out, and_191_out, and_201_out);
  xor xor_8 (xor_8_out, and_159_out, or_46_out);
  and and_193 (and_193_out, or_102_out, d_ff_75_q);
  and and_194 (and_194_out, or_78_out, or_55_out);
  and and_195 (and_195_out, or_58_out, d_ff_76_q);
  not not_55 (not_55_out, and_195_out);
  and and_196 (and_196_out, not_55_out, 1'b1, and_242_out);
  xor xor_9 (xor_9_out, and_191_out, and_201_out);
  and and_197 (and_197_out, or_101_out, and_217_out);
  D_Flip_Flop d_ff_77 (.D(and_197_out), .clk(and_177_out), .Q(d_ff_77_q));  // open: Qn, preset, reset
  and and_198 (and_198_out, or_102_out, d_ff_77_q);
  D_Flip_Flop d_ff_78 (.D(and_194_out), .clk(and_203_out), .Q(d_ff_78_q));  // open: Qn, preset, reset
  and and_199 (and_199_out, or_58_out, d_ff_78_q);
  not not_56 (not_56_out, and_199_out);
  and and_200 (and_200_out, not_56_out, 1'b1, and_242_out);
  and and_201 (and_201_out, and_196_out, and_209_out);
  not not_57 (not_57_out, and_152_out);
  and and_202 (and_202_out, and_178_out, not_57_out);
  not not_58 (not_58_out, and_202_out);
  not not_59 (not_59_out, xor_8_out);
  not not_60 (not_60_out, xor_6_out);
  not not_61 (not_61_out, xor_4_out);
  not not_62 (not_62_out, xor_2_out);
  D_Flip_Flop #(.trigger("high")) d_ff_79 (.D(xor_10_out), .clk(or_102_out), .Q(d_ff_79_q));  // open: Qn, preset, reset
  xor xor_10 (xor_10_out, and_188_out, and_208_out);
  and and_203 (and_203_out, or_78_out, and_167_out);
  xor xor_11 (xor_11_out, and_196_out, and_209_out);
  not not_63 (not_63_out, and_155_out);
  and and_204 (and_204_out, and_184_out, not_63_out);
  and and_205 (and_205_out, not_58_out, and_204_out);
  not not_64 (not_64_out, and_205_out);
  and and_206 (and_206_out, not_59_out, not_60_out, not_61_out, not_62_out);
  and and_207 (and_207_out, d_ff_79_q, or_100_out);
  and and_208 (and_208_out, and_193_out, and_216_out);
  and and_209 (and_209_out, and_200_out, and_213_out);
  not not_65 (not_65_out, and_158_out);
  and and_210 (and_210_out, and_195_out, not_65_out);
  and and_211 (and_211_out, not_64_out, and_210_out);
  and and_212 (and_212_out, d_ff_80_q, or_100_out);
  D_Flip_Flop #(.trigger("high")) d_ff_80 (.D(xor_12_out), .clk(or_102_out), .Q(d_ff_80_q));  // open: Qn, preset, reset
  xor xor_12 (xor_12_out, and_193_out, and_216_out);
  and and_213 (and_213_out, and_242_out, 1'b1, 1'b1);
  xor xor_13 (xor_13_out, and_200_out, and_213_out);
  not not_66 (not_66_out, and_159_out);
  and and_214 (and_214_out, and_199_out, not_66_out);
  and and_215 (and_215_out, not_67_out, and_214_out);
  not not_67 (not_67_out, and_211_out);
  xor xor_14 (xor_14_out, and_178_out, xor_2_out);
  not not_68 (not_68_out, xor_14_out);
  xor xor_15 (xor_15_out, and_151_out, and_178_out);
  D_Flip_Flop #(.trigger("high")) d_ff_81 (.D(xor_16_out), .clk(or_102_out), .Q(d_ff_81_q));  // open: Qn, preset, reset
  and and_216 (and_216_out, and_198_out, 1'b1);
  and and_217 (and_217_out, d_ff_81_q, or_100_out);
  xor xor_16 (xor_16_out, and_198_out, 1'b1);
  and and_218 (and_218_out, and_167_out, or_66_out);
  and and_219 (and_219_out, and_242_out, 1'b1, or_47_out);
  or or_47 (or_47_out, and_215_out, and_211_out, and_205_out, and_202_out);
  and and_220 (and_220_out, not_68_out, and_242_out, xor_15_out);
  and and_221 (and_221_out, or_66_out, or_52_out);
  D_Flip_Flop overflow (.D(and_221_out), .clk(and_218_out), .Q(overflow_q));  // open: Qn, preset, reset
  or or_48 (or_48_out, or_36_out, and_222_out);
  and and_222 (and_222_out, or_67_out, or_40_out);
  and and_223 (and_223_out, or_67_out, and_220_out);
  and and_224 (and_224_out, or_67_out, and_206_out);
  and and_225 (and_225_out, or_66_out, or_53_out);
  D_Flip_Flop signed_overflow (.D(and_225_out), .clk(and_218_out), .Q(signed_overflow_q));  // open: Qn, preset, reset
  // AND_Gate and_226 has open pins: in0=1'b0, in1=overflow_q, out=open
  or or_49 (or_49_out, or_37_out, and_223_out);
  or or_50 (or_50_out, or_38_out, and_224_out);
  or or_51 (or_51_out, or_39_out, and_227_out);
  and and_227 (and_227_out, or_67_out, and_219_out);
  // AND_Gate and_228 has open pins: in0=1'b0, in1=signed_overflow_q, out=open
  and and_229 (and_229_out, or_66_out, or_54_out);
  D_Flip_Flop zero (.D(and_229_out), .clk(and_218_out), .Q(zero_q));  // open: Qn, preset, reset
  // AND_Gate and_230 has open pins: in0=1'b0, in1=zero_q, out=open
  and and_231 (and_231_out, or_66_out, or_55_out);
  D_Flip_Flop negative (.D(and_231_out), .clk(and_218_out), .Q(negative_q));  // open: Qn, preset, reset
  // AND_Gate and_232 has open pins: in0=1'b0, in1=negative_q, out=open
  or or_52 (or_52_out, or_48_out, and_131_out);
  or or_53 (or_53_out, or_49_out, and_136_out);
  or or_54 (or_54_out, or_50_out, and_140_out);
  or or_55 (or_55_out, or_51_out, and_143_out);
  and and_233 (and_233_out, and_167_out, or_83_out);
  and and_234 (and_234_out, d_ff_85_q, and_257_out);
  and and_235 (and_235_out, or_83_out, and_131_out);
  D_Flip_Flop #(.trigger("high")) d_ff_82 (
    .D(and_235_out), .clk(and_233_out), .Q(d_ff_82_q));  // open: Qn, preset, reset
  not not_69 (not_69_out, d_ff_82_q);
  and Load (Load_out, not_69_out, not_70_out);
  and and_236 (and_236_out, Load_out, not_71_out);
  and and_237 (and_237_out, or_83_out, and_136_out);
  D_Flip_Flop #(.trigger("high")) d_ff_83 (
    .D(and_237_out), .clk(and_233_out), .Q(d_ff_83_q));  // open: Qn, preset, reset
  not not_70 (not_70_out, d_ff_83_q);
  not not_71 (not_71_out, Halt_out);
  and and_238 (and_238_out, or_83_out, and_140_out);
  D_Flip_Flop #(.trigger("high")) d_ff_84 (
    .D(and_238_out), .clk(and_233_out), .Q(d_ff_84_q));  // open: Qn, preset, reset
  not not_72 (not_72_out, d_ff_82_q);
  and Save (Save_out, not_72_out, d_ff_83_q);
  not not_73 (not_73_out, Halt_out);
  and and_239 (and_239_out, Save_out, not_73_out);
  and Add (Add_out, d_ff_82_q, not_75_out);
  not not_74 (not_74_out, Halt_out);
  and and_240 (and_240_out, Add_out, not_74_out);
  or or_56 (or_56_out, and_240_out, and_242_out);
  or or_57 (or_57_out, and_239_out, and_236_out, or_56_out);
  and and_241 (and_241_out, or_83_out, and_143_out);
  D_Flip_Flop #(.trigger("high")) d_ff_85 (
    .D(and_241_out), .clk(and_233_out), .Q(d_ff_85_q));  // open: Qn, preset, reset
  not not_75 (not_75_out, d_ff_83_q);
  and and_242 (and_242_out, Sub_out, not_76_out);
  and Sub (Sub_out, d_ff_82_q, d_ff_83_q);
  not not_76 (not_76_out, Halt_out);
  Clock clock_4 ();  // open: out
  and Halt (Halt_out, Sub_out, d_ff_84_q, d_ff_85_q);
  D_Flip_Flop d_ff_86 (.D(xor_17_out), .clk(and_167_out), .Q(d_ff_86_q));  // open: Qn, preset, reset
  D_Flip_Flop d_ff_87 (.D(xor_18_out), .clk(and_167_out), .Q(d_ff_87_q));  // open: Qn, preset, reset
  D_Flip_Flop d_ff_88 (.D(xor_19_out), .clk(and_167_out), .Q(d_ff_88_q));  // open: Qn, preset, reset
  D_Flip_Flop d_ff_89 (.D(xor_20_out), .clk(and_167_out), .Q(d_ff_89_q));  // open: Qn, preset, reset
  xor xor_17 (xor_17_out, d_ff_86_q, and_243_out);
  and and_243 (and_243_out, d_ff_87_q, and_244_out);
  xor xor_18 (xor_18_out, d_ff_87_q, and_244_out);
  not not_77 (not_77_out, d_ff_89_q);
  not not_78 (not_78_out, d_ff_86_q);
  not not_79 (not_79_out, d_ff_86_q);
  not not_80 (not_80_out, d_ff_89_q);
  not not_81 (not_81_out, d_ff_88_q);
  not not_82 (not_82_out, d_ff_87_q);
  not not_83 (not_83_out, d_ff_88_q);
  not not_84 (not_84_out, d_ff_87_q);
  not not_85 (not_85_out, d_ff_89_q);
  not not_86 (not_86_out, d_ff_86_q);
  not not_87 (not_87_out, d_ff_86_q);
  not not_88 (not_88_out, d_ff_89_q);
  not not_89 (not_89_out, d_ff_88_q);
  not not_90 (not_90_out, d_ff_87_q);
  not not_91 (not_91_out, d_ff_88_q);
  not not_92 (not_92_out, d_ff_87_q);
  not not_93 (not_93_out, d_ff_88_q);
  not not_94 (not_94_out, d_ff_87_q);
  not not_95 (not_95_out, d_ff_86_q);
  not not_96 (not_96_out, d_ff_89_q);
  not not_97 (not_97_out, d_ff_87_q);
  not not_98 (not_98_out, d_ff_86_q);
  not not_99 (not_99_out, d_ff_87_q);
  not not_100 (not_100_out, d_ff_86_q);
  not not_101 (not_101_out, d_ff_89_q);
  not not_102 (not_102_out, d_ff_88_q);
  not not_103 (not_103_out, d_ff_86_q);
  not not_104 (not_104_out, d_ff_88_q);
  not not_105 (not_105_out, d_ff_86_q);
  not not_106 (not_106_out, d_ff_88_q);
  not not_107 (not_107_out, d_ff_89_q);
  not not_108 (not_108_out, d_ff_89_q);
  not not_109 (not_109_out, d_ff_86_q);
  not not_110 (not_110_out, d_ff_86_q);
  not not_111 (not_111_out, d_ff_89_q);
  not not_112 (not_112_out, d_ff_88_q);
  not not_113 (not_113_out, d_ff_87_q);
  not not_114 (not_114_out, d_ff_88_q);
  not not_115 (not_115_out, d_ff_87_q);
  not not_116 (not_116_out, d_ff_89_q);
  not not_117 (not_117_out, d_ff_87_q);
  and and_244 (and_244_out, d_ff_88_q, and_262_out);
  and S0 (S0_out, not_77_out, d_ff_88_q, d_ff_87_q, not_78_out, or_56_out);
  and S1 (S1_out, d_ff_89_q, d_ff_88_q, d_ff_87_q, not_79_out, or_56_out);
  and S2 (S2_out, not_80_out, not_81_out, not_82_out, d_ff_86_q, or_56_out);
  and S3 (S3_out, d_ff_89_q, not_83_out, not_84_out, d_ff_86_q, or_56_out);
  and and_245 (and_245_out, not_85_out, d_ff_88_q, d_ff_87_q, not_86_out, and_239_out);
  and and_246 (and_246_out, d_ff_89_q, d_ff_88_q, d_ff_87_q, not_87_out, and_239_out);
  and and_247 (and_247_out, not_88_out, not_89_out, not_90_out, d_ff_86_q, and_239_out);
  and and_248 (and_248_out, d_ff_89_q, not_91_out, not_92_out, d_ff_86_q, and_239_out);
  and and_249 (and_249_out, d_ff_89_q, not_93_out, not_94_out, not_95_out, or_57_out);
  and and_250 (and_250_out, not_96_out, d_ff_88_q, not_97_out, not_98_out, or_57_out);
  and and_251 (and_251_out, d_ff_89_q, d_ff_88_q, not_99_out, not_100_out, or_57_out);
  and and_252 (and_252_out, not_101_out, not_102_out, d_ff_87_q, not_103_out, or_57_out);
  and and_253 (and_253_out, d_ff_89_q, not_104_out, d_ff_87_q, not_105_out, or_57_out);
  and and_254 (and_254_out, d_ff_89_q, not_106_out, d_ff_87_q, d_ff_86_q, or_57_out);
  and and_255 (and_255_out, not_107_out, d_ff_88_q, d_ff_87_q, d_ff_86_q, or_57_out);
  and and_256 (and_256_out, d_ff_89_q, d_ff_88_q, d_ff_87_q, d_ff_86_q, or_57_out);
  and and_257 (and_257_out, not_108_out, d_ff_88_q, d_ff_87_q, not_109_out, and_236_out);
  and and_258 (and_258_out, d_ff_89_q, d_ff_88_q, d_ff_87_q, not_110_out, and_236_out);
  and and_259 (and_259_out, not_111_out, not_112_out, not_113_out, d_ff_86_q, and_236_out);
  and and_260 (and_260_out, d_ff_89_q, not_114_out, not_115_out, d_ff_86_q, and_236_out);
  and and_261 (and_261_out, not_116_out, d_ff_88_q, not_117_out, d_ff_86_q, and_236_out);
  xor xor_19 (xor_19_out, d_ff_88_q, and_262_out);
  not not_118 (not_118_out, d_ff_84_q);
  not not_119 (not_119_out, d_ff_84_q);
  not not_120 (not_120_out, d_ff_84_q);
  and and_262 (and_262_out, d_ff_89_q, 1'b1);
  xor xor_20 (xor_20_out, d_ff_89_q, 1'b1);
  and and_263 (and_263_out, S1_out, not_118_out);
  and and_264 (and_264_out, and_246_out, not_119_out);
  and and_265 (and_265_out, and_261_out, not_120_out);
  and and_266 (and_266_out, S1_out, d_ff_84_q);
  or or_58 (or_58_out, 1'b0, S2_out);
  and and_267 (and_267_out, and_246_out, d_ff_84_q);
  and and_268 (and_268_out, and_261_out, d_ff_84_q);
  or or_59 (or_59_out, 1'b0, and_250_out);
  or or_60 (or_60_out, or_59_out, and_247_out);
  or or_61 (or_61_out, 1'b0, and_248_out);
  or or_62 (or_62_out, 1'b0, and_247_out);
  or or_63 (or_63_out, 1'b0, and_248_out);
  or or_64 (or_64_out, 1'b0, and_250_out, and_247_out);
  or or_65 (or_65_out, 1'b0, S0_out, and_263_out, and_264_out);
  or or_66 (or_66_out, 1'b0, S2_out);
  or or_67 (or_67_out, 1'b0, S2_out);
  or or_68 (or_68_out, 1'b0, and_249_out);
  or or_69 (or_69_out, 1'b0, and_249_out, and_245_out);
  or or_70 (or_70_out, 1'b0, S3_out);
  or or_71 (or_71_out, 1'b0, and_250_out, and_247_out);
  or or_72 (or_72_out, 1'b0, and_266_out, and_267_out);
  or or_73 (or_73_out, 1'b0, and_246_out);
  or or_74 (or_74_out, 1'b0, S0_out);
  or or_75 (or_75_out, 1'b0, and_247_out);
  or or_76 (or_76_out, 1'b0, S2_out);
  or or_77 (or_77_out, 1'b0, S3_out);
  or or_78 (or_78_out, 1'b0, S1_out);
  or or_79 (or_79_out, 1'b0, and_250_out);
  or or_80 (or_80_out, and_251_out, 1'b0);
  or or_81 (or_81_out, 1'b0, and_252_out);
  or or_82 (or_82_out, or_61_out, and_251_out);
  or or_83 (or_83_out, 1'b0, and_253_out);
  or or_84 (or_84_out, or_75_out, and_253_out);
  or or_85 (or_85_out, or_73_out, and_252_out);
  or or_86 (or_86_out, and_258_out, or_60_out);
  or or_87 (or_87_out, or_79_out, and_258_out);
  or or_88 (or_88_out, or_69_out, and_257_out);
  or or_89 (or_89_out, or_80_out, and_259_out);
  or or_90 (or_90_out, or_82_out, and_259_out);
  or or_91 (or_91_out, or_64_out, and_258_out);
  or or_92 (or_92_out, or_71_out, and_258_out);
  or or_93 (or_93_out, or_81_out, and_260_out);
  or or_94 (or_94_out, or_85_out, and_260_out);
  or or_95 (or_95_out, 1'b0, and_268_out);
  or or_96 (or_96_out, or_84_out, and_261_out);
  or or_97 (or_97_out, or_77_out, and_265_out);
  or or_98 (or_98_out, 1'b0, and_254_out);
  or or_99 (or_99_out, 1'b0, and_254_out);
  or or_100 (or_100_out, 1'b0, and_256_out);
  or or_101 (or_101_out, and_256_out, 1'b0);
  or or_102 (or_102_out, and_255_out, or_68_out);

  // Notes on the sheet:
  //   AR
  //   Mode
  //   Felipe Fontes - ID: 260976100
  //   Fabricio Dos Santos - ID: 260962607
  //   RAM
  //   DR
  //   D-Register
  //   Display
  //   U BUS
  //   Register 0
  //   MAR
  //   MBR
  //   Register 1
  //   L
  //   PC
  //   A-out
  //   R
  //   Inc
  //   ALU
  //   STATUS
  //   Control Unit
  //   IR
  //   Add/Sub micro-instructions
  //   Save micro-instructions
  //   Fetch micro-instructions
  //   Load micro-instructions
  //   Wires to AND gates
  //   D in
  //   RAM_0 out
  //   Inc out
  //   Change mode
  //   RAM in
  //   RAM out
  //   AR out
  //   DR in
  //   DR out
  //   AR in
  //   Mode RAM
  //   PC in
  //   PC out
  //   IR in
  //   MAR in
  //   MAR out
  //   MBR in
  //   MBR out
  //   R0 in
  //   R0 out
  //   R1 in
  //   R1 out 
  //   L in
  //   L out
  //   R in
  //   Sub Mode
  //   R out
  //   S in
  //   S out
  //   A in
  //   A out
  //   Display micro-instruction
  //   Increment PC
  //   Step incrementor
endmodule
